# Fritzing sketch schematic (saved by Fritzing 1.0.4)
breadboards: 2

parts:
  U1 = ESP32-38PinWide [part_number=ESP32-38PinWide]
  LCD1 = LCD screen  # not connected
  LCM1602_IIC1 = LCM1602 IIC [part_number="LCM1602 IIC" chip_label="LCM1602 IIC" package="DIP (Dual Inline) [THT]"]
  buz1 = Piezo Buzzer  # not connected
  LED1 = smd LED [color="Red (660nm)" package="0603 [SMD]"]
  S1 = Round Pushbutton
  R1 = Resistor [tolerance=±5% power=0.25W resistance=220 package=THT]
  R2 = Resistor [tolerance=±5% power=0.25W resistance=220 package=THT]

nets:
  N1: U1.GPIO21, LCM1602_IIC1.SDA
  N2: U1.GPIO22, LCM1602_IIC1.SCL
  N3: LCM1602_IIC1.GND, LED1.cathode, R2.Pin_0
  N4: LCM1602_IIC1.VCC, S1.leg0
  N5: LCM1602_IIC1.LED_A, LCM1602_IIC1.LED_B
  N6: LED1.anode, R1.Pin_0
  N7: S1.leg1, R2.Pin_1

custom parts:
  ESP32-38PinWide: Generic 38-Pin ESP32 with wide format (only access to one side of pins on a breadboard) based on Stephen Lilley's HiLetgo ESP-WROOM-32 ESP32 ESP-32S Development Board.
  LCM1602 IIC: I2C-Module to use a 1602 or 2004 LCD on with the wire.h libory Serial LCD Modul
  Piezo Buzzer: Part from https://www.nutsvolts.com/magazine/article/november2012_SmileysWorkshop. Breadboard and icon images modified to be 0.3" in spacing and be more similar to the actual physical part.
